// Logisim project 4BIT DISP FOR 0 TO 9.circ as structural Verilog: 9 circuits, main circuit main
module main (
  output out_1
);

  wire am_pm_toggle_1_ov, am_pm_toggle_1_r0, button_1_out, button_2_out, clock_1_out,
       encoder_using_for_weekday_counder_1_friday, encoder_using_for_weekday_counder_1_out_4,
       encoder_using_for_weekday_counder_1_out_5, encoder_using_for_weekday_counder_1_out_6,
       encoder_using_for_weekday_counder_1_out_7, encoder_using_for_weekday_counder_1_out_10,
       encoder_using_for_weekday_counder_1_out_11, encoder_using_for_weekday_counder_1_thursday,
       n0_5_counter_1_ov, n0_5_counter_1_r0, n0_5_counter_1_r1, n0_5_counter_1_r2, n0_5_counter_2_ov,
       n0_5_counter_2_r0, n0_5_counter_2_r1, n0_5_counter_2_r2, n0_9_counter_1_out_7, n0_9_counter_1_r0,
       n0_9_counter_1_r1, n0_9_counter_1_r2, n0_9_counter_1_r3, n0_9_counter_2_out_7, n0_9_counter_2_r0,
       n0_9_counter_2_r1, n0_9_counter_2_r2, n0_9_counter_2_r3, n1_12_counter_0000_t0_1011_1_out_7,
       n1_12_counter_0000_t0_1011_1_r0, n1_12_counter_0000_t0_1011_1_r1, n1_12_counter_0000_t0_1011_1_r2,
       n1_12_counter_0000_t0_1011_1_r3,
       n4_bit_display_driver_for_a_7_segment_display_counting_from_12_1_2_11_or_0000_to_1011_1_out_5,
       n4_bit_display_driver_for_a_7_segment_display_counting_from_12_1_2_11_or_0000_to_1011_1_out_6,
       n4_bit_display_driver_for_a_7_segment_display_counting_from_12_1_2_11_or_0000_to_1011_1_out_7,
       n4_bit_display_driver_for_a_7_segment_display_counting_from_12_1_2_11_or_0000_to_1011_1_out_8,
       n4_bit_display_driver_for_a_7_segment_display_counting_from_12_1_2_11_or_0000_to_1011_1_out_9,
       n4_bit_display_driver_for_a_7_segment_display_counting_from_12_1_2_11_or_0000_to_1011_1_out_10,
       n4_bit_display_driver_for_a_7_segment_display_counting_from_12_1_2_11_or_0000_to_1011_1_out_11,
       n4_bit_display_driver_for_a_7_segment_display_counting_from_12_1_2_11_or_0000_to_1011_1_out_12,
       n4_bit_driver_for_a_7_segment_display_from_0_9_0r_0000_to_10001_1_out_5,
       n4_bit_driver_for_a_7_segment_display_from_0_9_0r_0000_to_10001_1_out_6,
       n4_bit_driver_for_a_7_segment_display_from_0_9_0r_0000_to_10001_1_out_7,
       n4_bit_driver_for_a_7_segment_display_from_0_9_0r_0000_to_10001_1_out_8,
       n4_bit_driver_for_a_7_segment_display_from_0_9_0r_0000_to_10001_1_out_9,
       n4_bit_driver_for_a_7_segment_display_from_0_9_0r_0000_to_10001_1_out_10,
       n4_bit_driver_for_a_7_segment_display_from_0_9_0r_0000_to_10001_1_out_11,
       n4_bit_driver_for_a_7_segment_display_from_0_9_0r_0000_to_10001_2_out_5,
       n4_bit_driver_for_a_7_segment_display_from_0_9_0r_0000_to_10001_2_out_6,
       n4_bit_driver_for_a_7_segment_display_from_0_9_0r_0000_to_10001_2_out_7,
       n4_bit_driver_for_a_7_segment_display_from_0_9_0r_0000_to_10001_2_out_8,
       n4_bit_driver_for_a_7_segment_display_from_0_9_0r_0000_to_10001_2_out_9,
       n4_bit_driver_for_a_7_segment_display_from_0_9_0r_0000_to_10001_2_out_10,
       n4_bit_driver_for_a_7_segment_display_from_0_9_0r_0000_to_10001_2_out_11,
       n4_bit_driver_for_a_7_segment_display_from_0_9_0r_0000_to_10001_3_out_5,
       n4_bit_driver_for_a_7_segment_display_from_0_9_0r_0000_to_10001_3_out_6,
       n4_bit_driver_for_a_7_segment_display_from_0_9_0r_0000_to_10001_3_out_7,
       n4_bit_driver_for_a_7_segment_display_from_0_9_0r_0000_to_10001_3_out_8,
       n4_bit_driver_for_a_7_segment_display_from_0_9_0r_0000_to_10001_3_out_9,
       n4_bit_driver_for_a_7_segment_display_from_0_9_0r_0000_to_10001_3_out_10,
       n4_bit_driver_for_a_7_segment_display_from_0_9_0r_0000_to_10001_3_out_11,
       n4_bit_driver_for_a_7_segment_display_from_0_9_0r_0000_to_10001_4_out_5,
       n4_bit_driver_for_a_7_segment_display_from_0_9_0r_0000_to_10001_4_out_6,
       n4_bit_driver_for_a_7_segment_display_from_0_9_0r_0000_to_10001_4_out_7,
       n4_bit_driver_for_a_7_segment_display_from_0_9_0r_0000_to_10001_4_out_8,
       n4_bit_driver_for_a_7_segment_display_from_0_9_0r_0000_to_10001_4_out_9,
       n4_bit_driver_for_a_7_segment_display_from_0_9_0r_0000_to_10001_4_out_10,
       n4_bit_driver_for_a_7_segment_display_from_0_9_0r_0000_to_10001_4_out_11, not_1_out,
       week_day_counter_or_toggle_using_jk_flipflops_1_r0,
       week_day_counter_or_toggle_using_jk_flipflops_1_r1, week_day_counter_or_toggle_using_jk_flipflops_1_r2;

  Button button_1 (.out(button_1_out));
  Button button_2 (.out(button_2_out));
  not not_1 (not_1_out, am_pm_toggle_1_r0);
  AM_PM_TOGGLE am_pm_toggle_1 (
    .CLOCK(n1_12_counter_0000_t0_1011_1_out_7), .CLEAR(button_2_out), .R0(am_pm_toggle_1_r0),
    .OV(am_pm_toggle_1_ov));
  LED led_1 (.in(not_1_out));
  LED led_2 (.in(am_pm_toggle_1_r0));
  WEEK_DAY_COUNTER_OR_TOGGLE_USING_JK_FLIPFLOPS week_day_counter_or_toggle_using_jk_flipflops_1 (
    .CLOCK(am_pm_toggle_1_ov), .CLEAR(button_2_out), .R0(week_day_counter_or_toggle_using_jk_flipflops_1_r0),
    .R1(week_day_counter_or_toggle_using_jk_flipflops_1_r1),
    .R2(week_day_counter_or_toggle_using_jk_flipflops_1_r2), .OV(out_1));
  _1_12_COUNTER_0000_T0_1011 u_1_12_counter_0000_t0_1011_1 (
    .CLOCK(n0_5_counter_1_ov), .CLEAR(button_2_out), .R0(n1_12_counter_0000_t0_1011_1_r0),
    .R1(n1_12_counter_0000_t0_1011_1_r1), .R2(n1_12_counter_0000_t0_1011_1_r2),
    .R3(n1_12_counter_0000_t0_1011_1_r3), .out_7(n1_12_counter_0000_t0_1011_1_out_7));
  ENCODER_USING_FOR_WEEKDAY_COUNDER encoder_using_for_weekday_counder_1 (
    .C(week_day_counter_or_toggle_using_jk_flipflops_1_r2),
    .B(week_day_counter_or_toggle_using_jk_flipflops_1_r0),
    .A(week_day_counter_or_toggle_using_jk_flipflops_1_r1),
    .out_4(encoder_using_for_weekday_counder_1_out_4), .out_5(encoder_using_for_weekday_counder_1_out_5),
    .out_6(encoder_using_for_weekday_counder_1_out_6), .out_7(encoder_using_for_weekday_counder_1_out_7),
    .THURSDAY(encoder_using_for_weekday_counder_1_thursday),
    .FRIDAY(encoder_using_for_weekday_counder_1_friday), .out_10(encoder_using_for_weekday_counder_1_out_10),
    .out_11(encoder_using_for_weekday_counder_1_out_11));
  _4_BIT_DISPLAY_DRIVER_FOR_A_7_SEGMENT_DISPLAY_COUNTING_FROM_12__1_2____11_OR_0000_TO_1011 u_4_bit_display_driver_for_a_7_segment_display_counting_from_12_1_2_11_or_0000_to_1011_1 (
    .A(n1_12_counter_0000_t0_1011_1_r0), .B(n1_12_counter_0000_t0_1011_1_r1),
    .C(n1_12_counter_0000_t0_1011_1_r2), .D(n1_12_counter_0000_t0_1011_1_r3),
    .out_5(n4_bit_display_driver_for_a_7_segment_display_counting_from_12_1_2_11_or_0000_to_1011_1_out_5),
    .out_6(n4_bit_display_driver_for_a_7_segment_display_counting_from_12_1_2_11_or_0000_to_1011_1_out_6),
    .out_7(n4_bit_display_driver_for_a_7_segment_display_counting_from_12_1_2_11_or_0000_to_1011_1_out_7),
    .out_8(n4_bit_display_driver_for_a_7_segment_display_counting_from_12_1_2_11_or_0000_to_1011_1_out_8),
    .out_9(n4_bit_display_driver_for_a_7_segment_display_counting_from_12_1_2_11_or_0000_to_1011_1_out_9),
    .out_10(n4_bit_display_driver_for_a_7_segment_display_counting_from_12_1_2_11_or_0000_to_1011_1_out_10),
    .out_11(n4_bit_display_driver_for_a_7_segment_display_counting_from_12_1_2_11_or_0000_to_1011_1_out_11),
    .out_12(n4_bit_display_driver_for_a_7_segment_display_counting_from_12_1_2_11_or_0000_to_1011_1_out_12));
  _7_Segment_Display u_7_segment_display_1 (
    .b(n4_bit_display_driver_for_a_7_segment_display_counting_from_12_1_2_11_or_0000_to_1011_1_out_12),
    .c(n4_bit_display_driver_for_a_7_segment_display_counting_from_12_1_2_11_or_0000_to_1011_1_out_12));  // open: g, f, a, e, d, dp
  LED led_3 (.in(encoder_using_for_weekday_counder_1_out_4));
  _7_Segment_Display u_7_segment_display_2 (
    .g(n4_bit_display_driver_for_a_7_segment_display_counting_from_12_1_2_11_or_0000_to_1011_1_out_11),
    .f(n4_bit_display_driver_for_a_7_segment_display_counting_from_12_1_2_11_or_0000_to_1011_1_out_10),
    .a(n4_bit_display_driver_for_a_7_segment_display_counting_from_12_1_2_11_or_0000_to_1011_1_out_5),
    .b(n4_bit_display_driver_for_a_7_segment_display_counting_from_12_1_2_11_or_0000_to_1011_1_out_6),
    .e(n4_bit_display_driver_for_a_7_segment_display_counting_from_12_1_2_11_or_0000_to_1011_1_out_9),
    .d(n4_bit_display_driver_for_a_7_segment_display_counting_from_12_1_2_11_or_0000_to_1011_1_out_8),
    .c(n4_bit_display_driver_for_a_7_segment_display_counting_from_12_1_2_11_or_0000_to_1011_1_out_7));  // open: dp
  LED led_4 (.in(encoder_using_for_weekday_counder_1_out_6));
  LED led_5 (.in(encoder_using_for_weekday_counder_1_out_5));
  _0_5_COUNTER u_0_5_counter_1 (
    .CLOCK(n0_9_counter_1_out_7), .CLEAR(button_2_out), .R0(n0_5_counter_1_r0), .R1(n0_5_counter_1_r1),
    .R2(n0_5_counter_1_r2), .OV(n0_5_counter_1_ov));
  LED led_6 (.in(encoder_using_for_weekday_counder_1_out_7));
  _4_BIT_DRIVER_FOR_A_7_SEGMENT_DISPLAY_FROM_0_9_0R_0000_TO_10001 u_4_bit_driver_for_a_7_segment_display_from_0_9_0r_0000_to_10001_1 (
    .A(n0_5_counter_1_r0), .B(n0_5_counter_1_r1), .C(n0_5_counter_1_r2), .D(1'b0),
    .out_5(n4_bit_driver_for_a_7_segment_display_from_0_9_0r_0000_to_10001_1_out_5),
    .out_6(n4_bit_driver_for_a_7_segment_display_from_0_9_0r_0000_to_10001_1_out_6),
    .out_7(n4_bit_driver_for_a_7_segment_display_from_0_9_0r_0000_to_10001_1_out_7),
    .out_8(n4_bit_driver_for_a_7_segment_display_from_0_9_0r_0000_to_10001_1_out_8),
    .out_9(n4_bit_driver_for_a_7_segment_display_from_0_9_0r_0000_to_10001_1_out_9),
    .out_10(n4_bit_driver_for_a_7_segment_display_from_0_9_0r_0000_to_10001_1_out_10),
    .out_11(n4_bit_driver_for_a_7_segment_display_from_0_9_0r_0000_to_10001_1_out_11));
  _7_Segment_Display u_7_segment_display_3 (
    .g(n4_bit_driver_for_a_7_segment_display_from_0_9_0r_0000_to_10001_1_out_11),
    .f(n4_bit_driver_for_a_7_segment_display_from_0_9_0r_0000_to_10001_1_out_10),
    .a(n4_bit_driver_for_a_7_segment_display_from_0_9_0r_0000_to_10001_1_out_5),
    .b(n4_bit_driver_for_a_7_segment_display_from_0_9_0r_0000_to_10001_1_out_6),
    .e(n4_bit_driver_for_a_7_segment_display_from_0_9_0r_0000_to_10001_1_out_9),
    .d(n4_bit_driver_for_a_7_segment_display_from_0_9_0r_0000_to_10001_1_out_8),
    .c(n4_bit_driver_for_a_7_segment_display_from_0_9_0r_0000_to_10001_1_out_7));  // open: dp
  LED led_7 (.in(encoder_using_for_weekday_counder_1_thursday));
  _4_BIT_DRIVER_FOR_A_7_SEGMENT_DISPLAY_FROM_0_9_0R_0000_TO_10001 u_4_bit_driver_for_a_7_segment_display_from_0_9_0r_0000_to_10001_2 (
    .A(n0_9_counter_1_r0), .B(n0_9_counter_1_r1), .C(n0_9_counter_1_r2), .D(n0_9_counter_1_r3),
    .out_5(n4_bit_driver_for_a_7_segment_display_from_0_9_0r_0000_to_10001_2_out_5),
    .out_6(n4_bit_driver_for_a_7_segment_display_from_0_9_0r_0000_to_10001_2_out_6),
    .out_7(n4_bit_driver_for_a_7_segment_display_from_0_9_0r_0000_to_10001_2_out_7),
    .out_8(n4_bit_driver_for_a_7_segment_display_from_0_9_0r_0000_to_10001_2_out_8),
    .out_9(n4_bit_driver_for_a_7_segment_display_from_0_9_0r_0000_to_10001_2_out_9),
    .out_10(n4_bit_driver_for_a_7_segment_display_from_0_9_0r_0000_to_10001_2_out_10),
    .out_11(n4_bit_driver_for_a_7_segment_display_from_0_9_0r_0000_to_10001_2_out_11));
  _0_9_COUNTER u_0_9_counter_1 (
    .CLOCK(n0_5_counter_2_ov), .CLEAR(button_2_out), .R0(n0_9_counter_1_r0), .R1(n0_9_counter_1_r1),
    .R2(n0_9_counter_1_r2), .R3(n0_9_counter_1_r3), .out_7(n0_9_counter_1_out_7));
  LED led_8 (.in(encoder_using_for_weekday_counder_1_out_10));
  _7_Segment_Display u_7_segment_display_4 (
    .g(n4_bit_driver_for_a_7_segment_display_from_0_9_0r_0000_to_10001_2_out_11),
    .f(n4_bit_driver_for_a_7_segment_display_from_0_9_0r_0000_to_10001_2_out_10),
    .a(n4_bit_driver_for_a_7_segment_display_from_0_9_0r_0000_to_10001_2_out_5),
    .b(n4_bit_driver_for_a_7_segment_display_from_0_9_0r_0000_to_10001_2_out_6),
    .e(n4_bit_driver_for_a_7_segment_display_from_0_9_0r_0000_to_10001_2_out_9),
    .d(n4_bit_driver_for_a_7_segment_display_from_0_9_0r_0000_to_10001_2_out_8),
    .c(n4_bit_driver_for_a_7_segment_display_from_0_9_0r_0000_to_10001_2_out_7));  // open: dp
  LED led_9 (.in(encoder_using_for_weekday_counder_1_friday));
  _0_5_COUNTER u_0_5_counter_2 (
    .CLOCK(n0_9_counter_2_out_7), .CLEAR(button_2_out), .R0(n0_5_counter_2_r0), .R1(n0_5_counter_2_r1),
    .R2(n0_5_counter_2_r2), .OV(n0_5_counter_2_ov));
  _7_Segment_Display u_7_segment_display_5 (
    .g(n4_bit_driver_for_a_7_segment_display_from_0_9_0r_0000_to_10001_3_out_11),
    .f(n4_bit_driver_for_a_7_segment_display_from_0_9_0r_0000_to_10001_3_out_10),
    .a(n4_bit_driver_for_a_7_segment_display_from_0_9_0r_0000_to_10001_3_out_5),
    .b(n4_bit_driver_for_a_7_segment_display_from_0_9_0r_0000_to_10001_3_out_6),
    .e(n4_bit_driver_for_a_7_segment_display_from_0_9_0r_0000_to_10001_3_out_9),
    .d(n4_bit_driver_for_a_7_segment_display_from_0_9_0r_0000_to_10001_3_out_8),
    .c(n4_bit_driver_for_a_7_segment_display_from_0_9_0r_0000_to_10001_3_out_7));  // open: dp
  _4_BIT_DRIVER_FOR_A_7_SEGMENT_DISPLAY_FROM_0_9_0R_0000_TO_10001 u_4_bit_driver_for_a_7_segment_display_from_0_9_0r_0000_to_10001_3 (
    .A(n0_5_counter_2_r0), .B(n0_5_counter_2_r1), .C(n0_5_counter_2_r2), .D(1'b0),
    .out_5(n4_bit_driver_for_a_7_segment_display_from_0_9_0r_0000_to_10001_3_out_5),
    .out_6(n4_bit_driver_for_a_7_segment_display_from_0_9_0r_0000_to_10001_3_out_6),
    .out_7(n4_bit_driver_for_a_7_segment_display_from_0_9_0r_0000_to_10001_3_out_7),
    .out_8(n4_bit_driver_for_a_7_segment_display_from_0_9_0r_0000_to_10001_3_out_8),
    .out_9(n4_bit_driver_for_a_7_segment_display_from_0_9_0r_0000_to_10001_3_out_9),
    .out_10(n4_bit_driver_for_a_7_segment_display_from_0_9_0r_0000_to_10001_3_out_10),
    .out_11(n4_bit_driver_for_a_7_segment_display_from_0_9_0r_0000_to_10001_3_out_11));
  Clock clock_1 (.out(clock_1_out));
  _4_BIT_DRIVER_FOR_A_7_SEGMENT_DISPLAY_FROM_0_9_0R_0000_TO_10001 u_4_bit_driver_for_a_7_segment_display_from_0_9_0r_0000_to_10001_4 (
    .A(n0_9_counter_2_r0), .B(n0_9_counter_2_r1), .C(n0_9_counter_2_r2), .D(n0_9_counter_2_r3),
    .out_5(n4_bit_driver_for_a_7_segment_display_from_0_9_0r_0000_to_10001_4_out_5),
    .out_6(n4_bit_driver_for_a_7_segment_display_from_0_9_0r_0000_to_10001_4_out_6),
    .out_7(n4_bit_driver_for_a_7_segment_display_from_0_9_0r_0000_to_10001_4_out_7),
    .out_8(n4_bit_driver_for_a_7_segment_display_from_0_9_0r_0000_to_10001_4_out_8),
    .out_9(n4_bit_driver_for_a_7_segment_display_from_0_9_0r_0000_to_10001_4_out_9),
    .out_10(n4_bit_driver_for_a_7_segment_display_from_0_9_0r_0000_to_10001_4_out_10),
    .out_11(n4_bit_driver_for_a_7_segment_display_from_0_9_0r_0000_to_10001_4_out_11));
  _0_9_COUNTER u_0_9_counter_2 (
    .CLOCK(clock_1_out), .CLEAR(button_2_out), .R0(n0_9_counter_2_r0), .R1(n0_9_counter_2_r1),
    .R2(n0_9_counter_2_r2), .R3(n0_9_counter_2_r3), .out_7(n0_9_counter_2_out_7));
  _7_Segment_Display u_7_segment_display_6 (
    .g(n4_bit_driver_for_a_7_segment_display_from_0_9_0r_0000_to_10001_4_out_11),
    .f(n4_bit_driver_for_a_7_segment_display_from_0_9_0r_0000_to_10001_4_out_10),
    .a(n4_bit_driver_for_a_7_segment_display_from_0_9_0r_0000_to_10001_4_out_5),
    .b(n4_bit_driver_for_a_7_segment_display_from_0_9_0r_0000_to_10001_4_out_6),
    .e(n4_bit_driver_for_a_7_segment_display_from_0_9_0r_0000_to_10001_4_out_9),
    .d(n4_bit_driver_for_a_7_segment_display_from_0_9_0r_0000_to_10001_4_out_8),
    .c(n4_bit_driver_for_a_7_segment_display_from_0_9_0r_0000_to_10001_4_out_7));  // open: dp
  // also tied to GND on the sheet: encoder_using_for_weekday_counder_1_out_11

  // Notes on the sheet:
  //   AM PM TOGGLE
  //   RESET TIME TO 12 00 00
  //   AM
  //   PM
  //   1-12 COUNTER
  //   HOURS
  //   DISP 1
  //   SUNDAY
  //   MONDAY
  //   WEEK DAY COUNTER
  //   TUESDAY
  //   12 HOUR DIGITAL CLOCK WITH WEEKDAY COUNTER
  //   MINUTES
  //   WEDNESDAY
  //   DISP 2
  //   THURSDAY
  //   DISP 3
  //   FRIDAY
  //   SATURDAY
  //   DISP 4
  //   DISP 5
  //   SECONDS
endmodule

module _0_9_COUNTER (
  input  CLOCK,
  input  CLEAR,
  output R0,
  output R1,
  output R2,
  output R3,
  output out_7
);

  wire and_1_out, and_2_out, and_3_out, and_4_out, and_5_out, and_6_out, j_k_ff_4_qn, not_1_out, not_2_out,
       not_3_out, not_4_out;

  J_K_Flip_Flop j_k_ff_1 (.J(1'b1), .clk(CLOCK), .K(1'b1), .Q(R0), .reset(CLEAR));  // open: Qn, preset, en
  not not_1 (not_1_out, R0);
  and and_1 (and_1_out, 1'b1, not_1_out);
  and and_2 (and_2_out, R0, j_k_ff_4_qn);
  J_K_Flip_Flop j_k_ff_2 (.J(and_2_out), .clk(CLOCK), .K(R0), .Q(R1), .reset(CLEAR));  // open: Qn, preset, en
  not not_2 (not_2_out, R1);
  and and_3 (and_3_out, and_1_out, not_2_out);
  and and_4 (and_4_out, R1, R0);
  J_K_Flip_Flop j_k_ff_3 (.J(and_4_out), .clk(CLOCK), .K(and_4_out), .Q(R2), .reset(CLEAR));  // open: Qn, preset, en
  not not_3 (not_3_out, R2);
  and and_5 (and_5_out, and_3_out, not_3_out);
  and and_6 (and_6_out, R2, and_4_out);
  J_K_Flip_Flop j_k_ff_4 (
    .J(and_6_out), .clk(CLOCK), .K(R0), .Q(R3), .Qn(j_k_ff_4_qn), .reset(CLEAR));  // open: preset, en
  not not_4 (not_4_out, R3);
  and and_7 (out_7, and_5_out, not_4_out);

  // Notes on the sheet:
  //   A
  //   0 TO 9 COUNTER
  //   B
  //   C
  //   D
endmodule

module _4_BIT_DISPLAY_DRIVER_FOR_A_7_SEGMENT_DISPLAY_COUNTING_FROM_12__1_2____11_OR_0000_TO_1011 (
  input  A,
  input  B,
  input  C,
  input  D,
  output out_5,
  output out_6,
  output out_7,
  output out_8,
  output out_9,
  output out_10,
  output out_11,
  output out_12
);

  wire and_1_out, and_2_out, and_3_out, and_4_out, and_5_out, and_6_out, B_prime_A_prime_out, BA_out,
       BA_prime_out, C_prime_A_prime_out, CA_out, CA_prime_out, CB_prime_A_out, CB_prime_out,
       D_prime_C_prime_A_prime_B_prime_out, not_1_out, not_2_out, not_3_out, not_4_out;

  not not_1 (not_1_out, A);
  not not_2 (not_2_out, B);
  not not_3 (not_3_out, C);
  not not_4 (not_4_out, D);
  and D_prime_C_prime_A_prime_B_prime (D_prime_C_prime_A_prime_B_prime_out, not_3_out, not_1_out, not_2_out, not_4_out);
  and BA (BA_out, A, B);
  and B_prime_A_prime (B_prime_A_prime_out, not_2_out, not_1_out);
  and BA_prime (BA_prime_out, B, not_1_out);
  and CB_prime_A (CB_prime_A_out, C, not_2_out, A);
  and CA (CA_out, C, A);
  and CA_prime (CA_prime_out, C, not_1_out);
  and C_prime_A_prime (C_prime_A_prime_out, not_3_out, not_1_out);
  and CB_prime (CB_prime_out, C, not_2_out);
  and and_1 (and_1_out, not_3_out, B, not_4_out);
  and and_2 (and_2_out, not_1_out, not_4_out);
  and and_3 (and_3_out, B, not_4_out);
  and and_4 (and_4_out, not_2_out, D);
  and and_5 (and_5_out, not_1_out, D);
  and and_6 (and_6_out, B, D);
  or X (out_5, CA_out, and_3_out, and_4_out, C_prime_A_prime_out);
  or Y (out_6, BA_out, B_prime_A_prime_out, not_3_out);
  or Z (out_7, A, C, D);
  or U (out_8, CB_prime_A_out, BA_prime_out, C_prime_A_prime_out, and_1_out, and_4_out);
  or V (out_9, BA_prime_out, C_prime_A_prime_out);
  or W (out_10, CA_prime_out, CB_prime_out, and_4_out, and_5_out);
  or S (out_11, CB_prime_out, and_1_out, and_2_out, and_4_out);
  or T (out_12, D_prime_C_prime_A_prime_B_prime_out, and_6_out);

  // Notes on the sheet:
  //   C`
  //   B`
  //    B
  //   A`
  //   D
  //    D`
  //   4 BIT DISPLAY DRIVER FOR A 7 SEGMENT DISPLAY COUNTING FROM 12,1,2...12 (IC 4026)
endmodule

// OV
module _0_5_COUNTER (
  input  CLOCK,
  input  CLEAR,
  output R0,
  output R1,
  output R2,
  output OV
);

  wire and_1_out, and_2_out, and_3_out, and_4_out, C_qn, not_1_out, not_2_out, not_3_out;

  J_K_Flip_Flop A (.J(1'b1), .clk(CLOCK), .K(1'b1), .Q(R0), .reset(CLEAR));  // open: Qn, preset, en
  not not_1 (not_1_out, R0);
  and and_1 (and_1_out, 1'b1, not_1_out);
  and and_2 (and_2_out, R0, C_qn);
  J_K_Flip_Flop j_k_ff_1 (.J(and_2_out), .clk(CLOCK), .K(R0), .Q(R1), .reset(CLEAR));  // open: Qn, preset, en
  and and_3 (and_3_out, and_1_out, not_2_out);
  not not_2 (not_2_out, R1);
  and and_4 (and_4_out, R1, R0);
  J_K_Flip_Flop C (.J(and_4_out), .clk(CLOCK), .K(R0), .Q(R2), .Qn(C_qn), .reset(CLEAR));  // open: preset, en
  and and_5 (OV, and_3_out, not_3_out);
  not not_3 (not_3_out, R2);

  // Notes on the sheet:
  //   B
  //   0-5 COUNTER
endmodule

module _4_BIT_DRIVER_FOR_A_7_SEGMENT_DISPLAY_FROM_0_9_0R_0000_TO_10001 (
  input  A,
  input  B,
  input  C,
  input  D,
  output out_5,
  output out_6,
  output out_7,
  output out_8,
  output out_9,
  output out_10,
  output out_11
);

  wire and_1_out, and_2_out, and_3_out, and_4_out, and_5_out, and_6_out, and_7_out, and_8_out, and_9_out,
       not_1_out, not_2_out, not_3_out, not_4_out;

  not not_1 (not_1_out, A);
  not not_2 (not_2_out, B);
  not not_3 (not_3_out, C);
  not not_4 (not_4_out, D);
  and and_1 (and_1_out, B, A);
  and and_2 (and_2_out, not_2_out, not_1_out);
  and and_3 (and_3_out, B, not_1_out);
  and and_4 (and_4_out, C, not_2_out, A);
  and and_5 (and_5_out, C, A);
  and and_6 (and_6_out, C, not_1_out);
  and and_7 (and_7_out, not_3_out, not_1_out);
  and and_8 (and_8_out, C, not_2_out);
  and and_9 (and_9_out, not_3_out, B);
  or X (out_5, and_5_out, and_7_out, B, D);
  or Y (out_6, and_1_out, not_3_out, and_2_out);
  or Z (out_7, A, not_2_out, C, D);
  or U (out_8, and_3_out, and_4_out, and_7_out, and_9_out, D);
  or V (out_9, and_7_out, and_3_out);
  or W (out_10, and_2_out, and_6_out, and_8_out, D);
  or S (out_11, and_3_out, and_8_out, and_9_out, D);

  // Notes on the sheet:
  //   4BIT DRIVER FOR A 7 SEGMENT DISPLAY FROM 0-9
endmodule

module _1_12_COUNTER_0000_T0_1011 (
  input  CLOCK,
  input  CLEAR,
  output R0,
  output R1,
  output R2,
  output R3,
  output out_7
);

  wire and_1_out, and_2_out, and_3_out, and_4_out, and_5_out, and_6_out, j_k_ff_4_qn, not_1_out, not_2_out,
       not_3_out, not_4_out;

  J_K_Flip_Flop j_k_ff_1 (.J(1'b1), .clk(CLOCK), .K(1'b1), .Q(R0), .reset(CLEAR));  // open: Qn, preset, en
  not not_1 (not_1_out, R0);
  and and_1 (and_1_out, 1'b1, not_1_out);
  J_K_Flip_Flop j_k_ff_2 (.J(R0), .clk(CLOCK), .K(R0), .Q(R1), .reset(CLEAR));  // open: Qn, preset, en
  not not_2 (not_2_out, R1);
  and and_2 (and_2_out, and_1_out, not_2_out);
  and and_3 (and_3_out, R0, R1, j_k_ff_4_qn);
  and and_4 (and_4_out, R1, R0);
  not not_3 (not_3_out, R2);
  J_K_Flip_Flop j_k_ff_3 (.J(and_3_out), .clk(CLOCK), .K(and_4_out), .Q(R2), .reset(CLEAR));  // open: Qn, preset, en
  and and_5 (and_5_out, and_2_out, not_3_out);
  and and_6 (and_6_out, R1, R0, R2);
  J_K_Flip_Flop j_k_ff_4 (
    .J(and_6_out), .clk(CLOCK), .K(and_4_out), .Q(R3), .Qn(j_k_ff_4_qn), .reset(CLEAR));  // open: preset, en
  not not_4 (not_4_out, R3);
  and and_7 (out_7, and_5_out, not_4_out);

  // Notes on the sheet:
  //   1 TO 12 COUNTER USING JK FLIPFLOPS
endmodule

module AM_PM_TOGGLE (
  input  CLOCK,
  input  CLEAR,
  output R0,
  output OV
);

  wire not_1_out;

  J_K_Flip_Flop j_k_ff_1 (.J(1'b1), .clk(CLOCK), .K(1'b1), .Q(R0), .reset(CLEAR));  // open: Qn, preset, en
  not not_1 (not_1_out, R0);
  and and_1 (OV, 1'b1, not_1_out);

  // Notes on the sheet:
  //   AM PM TOGGLE
  //   A
endmodule

module WEEK_DAY_COUNTER_OR_TOGGLE_USING_JK_FLIPFLOPS (
  input  CLOCK,
  input  CLEAR,
  output R0,
  output R1,
  output R2,
  output OV
);

  wire and_1_out, and_2_out, and_3_out, j_k_ff_2_qn, j_k_ff_3_qn, not_1_out, not_2_out, not_3_out, or_1_out,
       or_2_out;

  or or_1 (or_1_out, j_k_ff_2_qn, j_k_ff_3_qn);
  J_K_Flip_Flop j_k_ff_1 (.J(or_1_out), .clk(CLOCK), .K(1'b1), .Q(R0), .reset(CLEAR));  // open: Qn, preset, en
  not not_1 (not_1_out, R0);
  and and_1 (and_1_out, 1'b1, not_1_out);
  or or_2 (or_2_out, R0, R2);
  J_K_Flip_Flop j_k_ff_2 (
    .J(R0), .clk(CLOCK), .K(or_2_out), .Q(R1), .Qn(j_k_ff_2_qn), .reset(CLEAR));  // open: preset, en
  not not_2 (not_2_out, R1);
  and and_2 (and_2_out, not_2_out, and_1_out);
  and and_3 (and_3_out, R0, R1);
  J_K_Flip_Flop j_k_ff_3 (
    .J(and_3_out), .clk(CLOCK), .K(R1), .Q(R2), .Qn(j_k_ff_3_qn), .reset(CLEAR));  // open: preset, en
  not not_3 (not_3_out, R2);
  and and_4 (OV, and_2_out, not_3_out);

  // Notes on the sheet:
  //   WEEKDAY COUNTER TOGGLE USING JK FLIPFLOP
  //   A
  //   B
  //   C
endmodule

module ENCODER_USING_FOR_WEEKDAY_COUNDER (
  input  C,
  input  B,
  input  A,
  output out_4,
  output out_5,
  output out_6,
  output out_7,
  output THURSDAY,
  output FRIDAY,
  output out_10,
  output out_11
);

  wire not_1_out, not_2_out, not_3_out;

  not not_1 (not_1_out, C);
  not not_2 (not_2_out, B);
  not not_3 (not_3_out, A);
  and and_1 (out_4, not_3_out, not_2_out, not_1_out);
  and and_2 (out_5, not_1_out, not_2_out, A);
  and and_3 (out_6, not_1_out, B, not_3_out);
  and and_4 (out_7, not_1_out, B, A);
  and and_5 (THURSDAY, C, not_2_out, not_3_out);
  and and_6 (FRIDAY, C, not_2_out, A);
  and and_7 (out_10, C, B, not_3_out);
  and and_8 (out_11, C, B, A);

  // Notes on the sheet:
  //   MSB
  //   3 TO 8 ENCODER FOR WEEKDAY COUNTRE 
  //   LSB
  //   SUNDAY
  //   MONDAY
  //   TUESDAY
  //   WEDNESDAY
  //   SATURDAY
endmodule
