// Logisim project AM PM TOGGLE.circ as structural Verilog: 9 circuits, main circuit main
module main (
);

  wire not_1_out, undriven;

  not not_1 (not_1_out, undriven);
  LED led_1 (.in(undriven));
  LED led_2 (.in(not_1_out));
endmodule

module _0_9_COUNTER (
  input  CLOCK,
  input  CLEAR,
  output R0,
  output R1,
  output R2,
  output R3,
  output out_7
);

  wire and_1_out, and_2_out, and_3_out, and_4_out, and_5_out, and_6_out, j_k_ff_4_qn, not_1_out, not_2_out,
       not_3_out, not_4_out;

  J_K_Flip_Flop j_k_ff_1 (.J(1'b1), .clk(CLOCK), .K(1'b1), .Q(R0), .reset(CLEAR));  // open: Qn, preset, en
  not not_1 (not_1_out, R0);
  and and_1 (and_1_out, 1'b1, not_1_out);
  and and_2 (and_2_out, R0, j_k_ff_4_qn);
  J_K_Flip_Flop j_k_ff_2 (.J(and_2_out), .clk(CLOCK), .K(R0), .Q(R1), .reset(CLEAR));  // open: Qn, preset, en
  not not_2 (not_2_out, R1);
  and and_3 (and_3_out, and_1_out, not_2_out);
  and and_4 (and_4_out, R1, R0);
  J_K_Flip_Flop j_k_ff_3 (.J(and_4_out), .clk(CLOCK), .K(and_4_out), .Q(R2), .reset(CLEAR));  // open: Qn, preset, en
  not not_3 (not_3_out, R2);
  and and_5 (and_5_out, and_3_out, not_3_out);
  and and_6 (and_6_out, R2, and_4_out);
  J_K_Flip_Flop j_k_ff_4 (
    .J(and_6_out), .clk(CLOCK), .K(R0), .Q(R3), .Qn(j_k_ff_4_qn), .reset(CLEAR));  // open: preset, en
  not not_4 (not_4_out, R3);
  and and_7 (out_7, and_5_out, not_4_out);

  // Notes on the sheet:
  //   A
  //   0 TO 9 COUNTER
endmodule

// OV
module _0_5_COUNTER (
  input  CLOCK,
  input  CLEAR,
  output R0,
  output R1,
  output R2,
  output OV
);

  wire and_1_out, and_2_out, and_3_out, and_4_out, C_qn, not_1_out, not_2_out, not_3_out;

  J_K_Flip_Flop A (.J(1'b1), .clk(CLOCK), .K(1'b1), .Q(R0), .reset(CLEAR));  // open: Qn, preset, en
  not not_1 (not_1_out, R0);
  and and_1 (and_1_out, 1'b1, not_1_out);
  and and_2 (and_2_out, R0, C_qn);
  J_K_Flip_Flop B (.J(and_2_out), .clk(CLOCK), .K(R0), .Q(R1), .reset(CLEAR));  // open: Qn, preset, en
  and and_3 (and_3_out, and_1_out, not_2_out);
  not not_2 (not_2_out, R1);
  and and_4 (and_4_out, R1, R0);
  J_K_Flip_Flop C (.J(and_4_out), .clk(CLOCK), .Q(R2), .Qn(C_qn), .reset(CLEAR));  // open: K, preset, en
  and and_5 (OV, and_3_out, not_3_out);
  not not_3 (not_3_out, R2);

  // Notes on the sheet:
  //   0-5 COUNTER
endmodule

module _4_BIT_DRIVER_FOR_A_7_SEGMENT_DISPLAY_FROM_0_9_0R_0000_TO_10001 (
  input  A,
  input  B,
  input  C,
  input  D,
  output out_5,
  output out_6,
  output out_7,
  output out_8,
  output out_9,
  output out_10,
  output out_11
);

  wire and_1_out, and_2_out, and_3_out, and_4_out, and_5_out, and_6_out, and_7_out, and_8_out, and_9_out,
       not_1_out, not_2_out, not_3_out;

  not not_1 (not_1_out, A);
  not not_2 (not_2_out, B);
  not not_3 (not_3_out, C);
  and and_1 (and_1_out, B, A);
  and and_2 (and_2_out, not_2_out, not_1_out);
  and and_3 (and_3_out, B, not_1_out);
  and and_4 (and_4_out, C, not_2_out, A);
  and and_5 (and_5_out, C, A);
  and and_6 (and_6_out, C, not_1_out);
  and and_7 (and_7_out, not_3_out, not_1_out);
  and and_8 (and_8_out, C, not_2_out);
  and and_9 (and_9_out, not_3_out, B);
  or or_1 (out_5, and_5_out, and_7_out, B, D);
  or or_2 (out_6, and_1_out, not_3_out, and_2_out);
  or or_3 (out_7, A, not_2_out, C, D);
  or or_4 (out_8, and_3_out, and_4_out, and_7_out, and_9_out, D);
  or or_5 (out_9, and_7_out, and_3_out);
  or or_6 (out_10, and_2_out, and_6_out, and_8_out, D);
  or or_7 (out_11, and_3_out, and_8_out, and_9_out, D);

  // Notes on the sheet:
  //   4BIT DRIVER FOR A 7 SEGMENT DISPLAY FROM 0-9
endmodule

module _4_BIT_DISPLAY_DRIVER_FOR_A_7_SEGMENT_DISPLAY_COUNTING_FROM_12__1_2____11_OR_0000_TO_1011 (
  input  A,
  input  B,
  input  C,
  input  D,
  output out_5,
  output out_6,
  output out_7,
  output out_8,
  output out_9,
  output out_10,
  output out_11,
  output out_12
);

  wire and_1_out, and_2_out, and_3_out, and_4_out, and_5_out, and_6_out, and_7_out, and_8_out, and_9_out,
       and_10_out, and_11_out, and_12_out, and_13_out, and_15_out, not_1_out, not_2_out, not_3_out, not_4_out;

  not not_1 (not_1_out, A);
  not not_2 (not_2_out, B);
  not not_3 (not_3_out, C);
  not not_4 (not_4_out, D);
  and and_1 (and_1_out, not_4_out, not_3_out, not_2_out, not_1_out);
  and and_2 (and_2_out, B, A);
  and and_3 (and_3_out, not_4_out, not_3_out, B);
  and and_4 (and_4_out, not_2_out, not_1_out);
  and and_5 (and_5_out, B, not_1_out);
  and and_6 (and_6_out, not_4_out, not_1_out);
  and and_7 (and_7_out, C, not_2_out, A);
  and and_8 (and_8_out, not_4_out, not_2_out);
  and and_9 (and_9_out, C, A);
  and and_10 (and_10_out, C, not_1_out);
  and and_11 (and_11_out, not_3_out, not_1_out);
  and and_12 (and_12_out, D, not_2_out);
  and and_13 (and_13_out, C, not_2_out);
  // AND_Gate and_14 has open pins: in0=D, in1=not_1_out, out=open
  and and_15 (and_15_out, D, B);
  or or_1 (out_5, and_9_out, and_8_out, and_12_out, and_11_out);
  or or_2 (out_6, and_2_out, and_4_out, not_3_out);
  or or_3 (out_7, A, C, D);
  or or_4 (out_8, and_7_out, and_5_out, and_11_out, and_3_out, and_12_out);
  or or_5 (out_9, and_5_out, and_11_out);
  or or_6 (out_10, and_10_out, and_13_out, and_12_out);
  or or_7 (out_11, and_13_out, and_3_out, and_6_out, and_12_out);
  or or_8 (out_12, and_1_out, and_15_out);

  // Notes on the sheet:
  //   C
  //   C`
  //   B`
  //   A`
  //   B
  //   A
  //   D`
  //   D
endmodule

module _1_12_COUNTER_0000_T0_1011 (
  input  in_1,
  input  in_2,
  output out_3,
  output out_4,
  output out_5,
  output out_6,
  output out_7
);

  wire and_1_out, and_2_out, and_3_out, and_4_out, and_5_out, and_6_out, j_k_ff_4_qn, not_1_out, not_2_out,
       not_3_out, not_4_out;

  J_K_Flip_Flop j_k_ff_1 (.J(1'b1), .clk(in_1), .K(1'b1), .Q(out_3), .reset(in_2));  // open: Qn, preset, en
  not not_1 (not_1_out, out_3);
  and and_1 (and_1_out, 1'b1, not_1_out);
  J_K_Flip_Flop j_k_ff_2 (.J(out_3), .clk(in_1), .K(out_3), .Q(out_4), .reset(in_2));  // open: Qn, preset, en
  not not_2 (not_2_out, out_4);
  and and_2 (and_2_out, and_1_out, not_2_out);
  and and_3 (and_3_out, out_3, out_4, j_k_ff_4_qn);
  and and_4 (and_4_out, out_4, out_3);
  not not_3 (not_3_out, out_5);
  J_K_Flip_Flop j_k_ff_3 (.J(and_3_out), .clk(in_1), .K(and_4_out), .Q(out_5), .reset(in_2));  // open: Qn, preset, en
  and and_5 (and_5_out, and_2_out, not_3_out);
  and and_6 (and_6_out, out_4, out_3, out_5);
  J_K_Flip_Flop j_k_ff_4 (
    .J(and_6_out), .clk(in_1), .K(and_4_out), .Q(out_6), .Qn(j_k_ff_4_qn), .reset(in_2));  // open: preset, en
  not not_4 (not_4_out, out_6);
  and and_7 (out_7, and_5_out, not_4_out);
endmodule

module AM___PM_TOGGLE (
  input  in_1,
  input  in_2,
  output out_3,
  output out_4
);

  wire not_1_out;

  J_K_Flip_Flop j_k_ff_1 (.J(1'b1), .clk(in_1), .K(1'b1), .Q(out_3), .reset(in_2));  // open: Qn, preset, en
  not not_1 (not_1_out, out_3);
  and and_1 (out_4, 1'b1, not_1_out);
endmodule

module WEEK_DAY_COUNTER_OR_TOGGLE_USING_JK_FLIPFLOPS (
  input  in_1,
  input  in_2,
  output out_3,
  output out_4,
  output out_5,
  output out_6
);

  wire and_1_out, and_2_out, and_3_out, j_k_ff_2_qn, j_k_ff_3_qn, not_1_out, not_2_out, not_3_out, or_1_out,
       or_2_out;

  or or_1 (or_1_out, j_k_ff_2_qn, j_k_ff_3_qn);
  J_K_Flip_Flop j_k_ff_1 (.J(or_1_out), .clk(in_1), .K(1'b1), .Q(out_3), .reset(in_2));  // open: Qn, preset, en
  not not_1 (not_1_out, out_3);
  and and_1 (and_1_out, 1'b1, not_1_out);
  or or_2 (or_2_out, out_3, out_5);
  J_K_Flip_Flop j_k_ff_2 (
    .J(out_3), .clk(in_1), .K(or_2_out), .Q(out_4), .Qn(j_k_ff_2_qn), .reset(in_2));  // open: preset, en
  not not_2 (not_2_out, out_4);
  and and_2 (and_2_out, not_2_out, and_1_out);
  and and_3 (and_3_out, out_3, out_4);
  J_K_Flip_Flop j_k_ff_3 (
    .J(and_3_out), .clk(in_1), .K(out_4), .Q(out_5), .Qn(j_k_ff_3_qn), .reset(in_2));  // open: preset, en
  not not_3 (not_3_out, out_5);
  and and_4 (out_6, and_2_out, not_3_out);
endmodule

module ENCODER_USING_FOR_WEEKDAY_COUNDER (
  input  C,
  input  A,
  input  B,
  output out_4,
  output out_5,
  output out_6,
  output out_7,
  output out_8,
  output out_9,
  output out_10,
  output out_11
);

  wire not_1_out, not_2_out, not_3_out;

  not not_1 (not_1_out, C);
  not not_2 (not_2_out, A);
  not not_3 (not_3_out, B);
  and and_1 (out_4, not_2_out, not_1_out, not_3_out);
  and and_2 (out_5, not_1_out, not_2_out, B);
  and and_3 (out_6, not_1_out, A, not_3_out);
  and and_4 (out_7, not_1_out, A, B);
  and and_5 (out_8, C, not_2_out, not_3_out);
  and and_6 (out_9, C, not_2_out, B);
  and and_7 (out_10, C, A, not_3_out);
  and and_8 (out_11, C, A, B);
endmodule
